// Logisim project aiAlu.circ as structural Verilog: 12 circuits, main circuit aiALU
module aiALU (
  input  [7:0] A,
  input  [7:0] B,
  input  [2:0] Select,
  output [7:0] Output,
  output Overflow,
  output Carry
);

  wire nand_1_out, not_1_out, not_2_out;
  wire [1:0] bit_extender_1_out;
  wire [7:0] aiarith_1_out, ailogic_1_out;

  // Probe on A
  // Probe on B
  aiArith aiarith_1 (
    .A(A), .B(B), .Select(Select[0]), .Out(aiarith_1_out), .Overflow_Check(Overflow), .Carry_Out(Carry));
  aiLogic ailogic_1 (.in_1(Select), .A(B), .B(A), .Out(ailogic_1_out));
  not not_1 (not_1_out, Select[1]);
  not not_2 (not_2_out, Select[2]);
  nand nand_1 (nand_1_out, not_1_out, not_2_out);
  // Probe on Output
  MUX8data mux8data_1 (.A(aiarith_1_out), .B(ailogic_1_out), .Select(bit_extender_1_out), .Y(Output));  // open: C, D
  assign bit_extender_1_out = {{1{1'b0}}, nand_1_out};  // Bit_Extender bit_extender_1

  // Notes on the sheet:
  //   000: A + B
  //   001: A - B
  //   010: A & B
  //   011: A | B
  //   100: A xor B
  //   101: !A
  //   110: !B
  //   111: 0
endmodule

module aiArith (
  input  [7:0] A,
  input  [7:0] B,
  input  Select,
  output [7:0] Out,
  output Overflow_Check,
  output Carry_Out
);

  wire [1:0] aisum_1_carry_out, aisum_1_overflow, bit_extender_1_out;
  wire [7:0] aisum_1_sum, aisum_2_sum, twocomplement_1_out;

  // Probe on A
  // Probe on B
  twoComplement twocomplement_1 (.In(B), .Out(twocomplement_1_out));
  assign bit_extender_1_out = {{1{1'b0}}, Select};  // Bit_Extender bit_extender_1
  aiSum aisum_1 (
    .Carry_In(1'b0), .A(A), .B(B), .Sum(aisum_1_sum), .Overflow(aisum_1_overflow[0]),
    .Carry_Out(aisum_1_carry_out[0]));
  aiSum aisum_2 (
    .Carry_In(1'b0), .A(A), .B(twocomplement_1_out), .Sum(aisum_2_sum), .Overflow(aisum_1_overflow[1]),
    .Carry_Out(aisum_1_carry_out[1]));
  MUX8data mux8data_1 (
    .A(aisum_1_sum), .B(aisum_2_sum), .C({8{1'b0}}), .D({8{1'b0}}), .Select(bit_extender_1_out), .Y(Out));
  MUX_4_inputs mux_4_inputs_1 (.Select(bit_extender_1_out), .Data({2'b00, aisum_1_overflow}), .Output(Overflow_Check));
  MUX_4_inputs mux_4_inputs_2 (.Select(bit_extender_1_out), .Data({2'b00, aisum_1_carry_out}), .Output(Carry_Out));
  // Probe on Out

  // Notes on the sheet:
  //   A + B
  //   A - B
endmodule

module aiLogic (
  input  [2:0] in_1,
  input  [7:0] A,
  input  [7:0] B,
  output [7:0] Out
);

  wire [1:0] bit_extender_1_out;
  wire [7:0] and_1_out_3, mux8data_1_y, mux8data_2_y, not_1_out_2, not_2_out_2, or_1_out_3, xor_1_out_3;

  AND and_1 (.in_1(A), .in_2(B), .out_3(and_1_out_3));
  OR or_1 (.in_1(A), .in_2(B), .out_3(or_1_out_3));
  NOT not_1 (.in_1(B), .out_2(not_1_out_2));
  NOT not_2 (.in_1(A), .out_2(not_2_out_2));
  XOR xor_1 (.in_1(A), .in_2(B), .out_3(xor_1_out_3));
  MUX8data mux8data_1 (
    .A({8{1'b0}}), .B({8{1'b0}}), .C(and_1_out_3), .D(or_1_out_3), .Select(in_1[1:0]), .Y(mux8data_1_y));
  MUX8data mux8data_2 (
    .A(xor_1_out_3), .B(not_1_out_2), .C(not_2_out_2), .D({8{1'b0}}), .Select(in_1[1:0]), .Y(mux8data_2_y));
  assign bit_extender_1_out = {{1{1'b0}}, in_1[2]};  // Bit_Extender bit_extender_1
  MUX8data mux8data_3 (.A(mux8data_1_y), .B(mux8data_2_y), .Select(bit_extender_1_out), .Y(Out));  // open: C, D
endmodule

module MUX_4_inputs (
  input  [1:0] Select,
  input  [3:0] Data,
  output Output
);

  wire and_1_out, and_2_out, and_3_out, and_4_out, not_1_out, not_2_out, not_3_out, not_4_out;

  and and_1 (and_1_out, Select[0], Select[1], Data[3]);
  not not_1 (not_1_out, Select[0]);
  and and_2 (and_2_out, not_1_out, Select[1], Data[2]);
  not not_2 (not_2_out, Select[1]);
  and and_3 (and_3_out, Select[0], not_2_out, Data[1]);
  not not_3 (not_3_out, Select[0]);
  not not_4 (not_4_out, Select[1]);
  and and_4 (and_4_out, not_3_out, not_4_out, Data[0]);
  or or_1 (Output, and_1_out, and_2_out, and_3_out, and_4_out);
endmodule

module fullAdder (
  input  A,
  input  B,
  input  Carry_In,
  output Output,
  output Carry_Out
);

  wire and_1_out, and_2_out, and_3_out, xor_1_out;

  xor xor_1 (xor_1_out, A, B);
  and and_1 (and_1_out, A, B);
  and and_2 (and_2_out, B, Carry_In);
  and and_3 (and_3_out, A, Carry_In);
  xor xor_2 (Output, xor_1_out, Carry_In);
  or or_1 (Carry_Out, and_1_out, and_2_out, and_3_out);
endmodule

module aiSum (
  input  Carry_In,
  input  [7:0] A,
  input  [7:0] B,
  output [7:0] Sum,
  output Overflow,
  output Carry_Out
);

  wire and_1_out, and_2_out, and_3_out, and_4_out, fulladder_1_carry_out, fulladder_2_carry_out,
       fulladder_3_carry_out, fulladder_4_carry_out, fulladder_5_carry_out, fulladder_6_carry_out,
       fulladder_7_carry_out, not_1_out, not_2_out, not_3_out;

  and and_1 (and_1_out, A[7], B[7]);
  not not_1 (not_1_out, A[7]);
  and and_2 (and_2_out, not_1_out, not_2_out);
  not not_2 (not_2_out, B[7]);
  not not_3 (not_3_out, Sum[7]);
  and and_3 (and_3_out, not_3_out, and_1_out);
  and and_4 (and_4_out, Sum[7], and_2_out);
  fullAdder fulladder_1 (.A(A[0]), .B(B[0]), .Carry_In(Carry_In), .Output(Sum[0]), .Carry_Out(fulladder_1_carry_out));
  fullAdder fulladder_2 (
    .A(A[1]), .B(B[1]), .Carry_In(fulladder_1_carry_out), .Output(Sum[1]), .Carry_Out(fulladder_2_carry_out));
  fullAdder fulladder_3 (
    .A(A[2]), .B(B[2]), .Carry_In(fulladder_2_carry_out), .Output(Sum[2]), .Carry_Out(fulladder_3_carry_out));
  fullAdder fulladder_4 (
    .A(A[3]), .B(B[3]), .Carry_In(fulladder_3_carry_out), .Output(Sum[3]), .Carry_Out(fulladder_4_carry_out));
  fullAdder fulladder_5 (
    .A(A[4]), .B(B[4]), .Carry_In(fulladder_4_carry_out), .Output(Sum[4]), .Carry_Out(fulladder_5_carry_out));
  fullAdder fulladder_6 (
    .A(A[5]), .B(B[5]), .Carry_In(fulladder_5_carry_out), .Output(Sum[5]), .Carry_Out(fulladder_6_carry_out));
  fullAdder fulladder_7 (
    .A(A[6]), .B(B[6]), .Carry_In(fulladder_6_carry_out), .Output(Sum[6]), .Carry_Out(fulladder_7_carry_out));
  fullAdder fulladder_8 (.A(A[7]), .B(B[7]), .Carry_In(fulladder_7_carry_out), .Output(Sum[7]), .Carry_Out(Carry_Out));
  or or_1 (Overflow, and_3_out, and_4_out);
endmodule

module AND (
  input  [7:0] in_1,
  input  [7:0] in_2,
  output [7:0] out_3
);

  assign out_3 = in_1 & in_2;  // AND_Gate and_1, 8 bits wide
endmodule

module OR (
  input  [7:0] in_1,
  input  [7:0] in_2,
  output [7:0] out_3
);

  assign out_3 = in_1 | in_2;  // OR_Gate or_1, 8 bits wide
endmodule

module NOT (
  input  [7:0] in_1,
  output [7:0] out_2
);

  assign out_2 = ~in_1;  // NOT_Gate not_1, 8 bits wide
endmodule

module XOR (
  input  [7:0] in_1,
  input  [7:0] in_2,
  output [7:0] out_3
);

  assign out_3 = in_1 ^ in_2;  // XOR_Gate xor_1, 8 bits wide
endmodule

module twoComplement (
  input  [7:0] In,
  output [7:0] Out
);

  wire [7:0] not_1_out;

  not not_1 (not_1_out[0], In[0]);
  not not_2 (not_1_out[1], In[1]);
  not not_3 (not_1_out[2], In[2]);
  not not_4 (not_1_out[3], In[3]);
  not not_5 (not_1_out[4], In[4]);
  not not_6 (not_1_out[5], In[5]);
  not not_7 (not_1_out[6], In[6]);
  not not_8 (not_1_out[7], In[7]);
  aiSum aisum_1 (.Carry_In(1'b0), .A(not_1_out), .B(8'h1), .Sum(Out));  // open: Overflow, Carry_Out
endmodule

module MUX8data (
  input  [7:0] A,
  input  [7:0] B,
  input  [7:0] C,
  input  [7:0] D,
  input  [1:0] Select,
  output [7:0] Y
);

  MUX_4_inputs mux_4_inputs_1 (.Select(Select), .Data({D[0], C[0], B[0], A[0]}), .Output(Y[0]));
  MUX_4_inputs mux_4_inputs_2 (.Select(Select), .Data({D[1], C[1], B[1], A[1]}), .Output(Y[1]));
  MUX_4_inputs mux_4_inputs_3 (.Select(Select), .Data({D[2], C[2], B[2], A[2]}), .Output(Y[2]));
  MUX_4_inputs mux_4_inputs_4 (.Select(Select), .Data({D[3], C[3], B[3], A[3]}), .Output(Y[3]));
  MUX_4_inputs mux_4_inputs_5 (.Select(Select), .Data({D[4], C[4], B[4], A[4]}), .Output(Y[4]));
  MUX_4_inputs mux_4_inputs_6 (.Select(Select), .Data({D[5], C[5], B[5], A[5]}), .Output(Y[5]));
  MUX_4_inputs mux_4_inputs_7 (.Select(Select), .Data({D[6], C[6], B[6], A[6]}), .Output(Y[6]));
  MUX_4_inputs mux_4_inputs_8 (.Select(Select), .Data({D[7], C[7], B[7], A[7]}), .Output(Y[7]));

  // Other names for the same wires on the sheet: S[1:0] = Select
endmodule
